# Fritzing sketch NE555 (saved by Fritzing 0.9.10b)
circuit board: 4.84cm x 4.3cm
breadboards: 1

parts:
  NE555L = 555 Timer [package="DIP8 [THT]"]
  D1 = Rectifier Diode [part_number=1N4001 package="300 mil [THT]"]
  Ton1 = POT [knob_status=50% power=0.5W package=pot_alpha_rv16af-20]
  Toff1 = POT [knob_status=50% power=0.5W package=pot_alpha_rv16af-20]
  R_1kOhm = Resistor [tolerance=±5% power=0.25 resistance=220 package=THT]
  R_1kOhm_2 = Resistor [tolerance=±5% power=0.25 resistance=220 package=THT]
  GND_OUT = Camdenboss CTB0158-2 [part_number=CTB0158-2 package=THT]
  GND_+9V = Camdenboss CTB0158-2 [part_number=CTB0158-2 package=THT]
  C_100nF = Ceramic Capacitor [capacitance=100nF voltage=35V package="200 mil [THT, multilayer]"]
  C_100nF_2 = Ceramic Capacitor [capacitance=100nF voltage=35V package="200 mil [THT, multilayer]"]

nets:
  N1: NE555L.Ground, GND_OUT.pin2, GND_+9V.pin2, C_100nF.0, C_100nF_2.1
  N2: NE555L.Trigger, NE555L.Threshold, D1.cathode, R_1kOhm.Pin_1, C_100nF_2.0
  N3: NE555L.Output, GND_OUT.pin1
  N4: NE555L.Reset, NE555L.Vcc_Supply_Voltage, Ton1.E, GND_+9V.pin1
  N5: NE555L.Control_Voltage, C_100nF.1
  N6: NE555L.Discharge, D1.anode, Toff1.E, R_1kOhm_2.Pin_1
  N7: Ton1.S, R_1kOhm_2.Pin_0
  N8: Toff1.S, R_1kOhm.Pin_0
