# Fritzing sketch NE555_v2 (saved by Fritzing 1.0.3b)
circuit board: 3.2994cm x 3.8cm
breadboards: 1

parts:
  NE555L = 555 Timer [package="DIP8 [THT]"]
  D1 = Rectifier Diode [part_number=1N4001 package="300 mil [THT]"]
  R_1kOhm = Resistor [tolerance=±5% power=0.25 resistance=220 package=THT]
  R_1kOhm_2 = Resistor [tolerance=±5% power=0.25 resistance=220 package=THT]
  C_100nF = Ceramic Capacitor [capacitance=100nF voltage=35V package="200 mil [THT, multilayer]"]
  T_OFF = Trimpot-3296 [package=3386u]
  T_ON = Trimpot-3296 [package=3386u]
  J1 = Terminal Block - 2 pins [package=THT]
  J2 = Terminal Block - 2 pins [package=THT]
  C_100nF_2 = Ceramic Capacitor [capacitance=100nF voltage=35V package="200 mil [THT, multilayer]"]

nets:
  N1: NE555L.Ground, C_100nF.1, J1.Line_2, J2.Line_2, C_100nF_2.0
  N2: NE555L.Trigger, NE555L.Threshold, D1.cathode, R_1kOhm.Pin_1, C_100nF.0
  N3: NE555L.Output, J1.Line_1
  N4: NE555L.Reset, NE555L.Vcc_Supply_Voltage, T_ON.CCW, J2.Line_1
  N5: NE555L.Control_Voltage, C_100nF_2.1
  N6: NE555L.Discharge, D1.anode, R_1kOhm_2.Pin_1, T_OFF.CCW
  N7: R_1kOhm.Pin_0, T_OFF.WIPER
  N8: R_1kOhm_2.Pin_0, T_ON.WIPER

custom parts:
  Trimpot-3296: Trimpot 3296 / 25 turn stand
  Terminal Block - 2 pins: Generic Screw Terminal 8mm
