# Fritzing sketch aaaaa (saved by Fritzing 0.9.10b)
circuit board: 4.3cm x 4.3cm
breadboards: 1

parts:
  T_ON = Trimpot-3296 [package=3386u]
  J1 = female pin header, 1 pin [form="♀ (female)"]
  J2 = female pin header, 1 pin [form="♀ (female)"]

nets:
  N1: T_ON.CCW, J2.pin1
  N2: T_ON.WIPER, J1.pin1

custom parts:
  Trimpot-3296: Trimpot 3296 / 25 turn stand
