# Fritzing sketch AMPLIFICADOR (saved by Fritzing 1.0.3b)
circuit board: 5.07625cm x 3.42715cm
breadboards: 1

parts:
  J1 = male pin header, 2 pins [form="♂ (male)"]
  J2 = Terminal Block - 2 pins [package=THT]
  JACK_6_35MM = AMPHENOL - ACJS-MHDR [package=ACJS-MHDR]
  U1 = LM386 [package=dip08]
  R2 = Resistor [tolerance=±5% power=0.25W resistance=220 package=THT]
  C1 = Electrolytic Capacitor [capacitance=1µF voltage=35V package="100 mil [THT, electrolytic]"]
  C2 = Ceramic Capacitor [capacitance="100 nF" voltage=35V package="200 mil [THT, multilayer]"]
  VR1 = Trimpot-#3296-flat [package=3386u]
  C3 = Ceramic Capacitor [capacitance="100 nF" voltage=35V package="200 mil [THT, multilayer]"]
  R3 = Resistor [tolerance=±5% power=0.25W resistance=220 package=THT]
  C4 = Electrolytic Capacitor [capacitance=1µF voltage=35V package="100 mil [THT, electrolytic]"]
  J3 = Terminal Block - 2 pins [package=THT]

nets:
  N1: J1.pin1, U1.GAIN, R2.Pin_0, C1.-
  N2: J1.pin2, R2.Pin_1, C1.+
  N3: J2.Line_1, JACK_6_35MM.Sleeve_(4), U1.-IN, U1.V-, C2.0, VR1.CW, R3.Pin_1, J3.Line_1
  N4: J2.Line_2, U1.V+
  N5: JACK_6_35MM.Ring_(5), JACK_6_35MM.Tip_(6), VR1.CCW
  N6: U1.+IN, VR1.WIPER
  N7: U1.OUT, C3.1, C4.+
  N8: U1.BP, C2.1
  N9: C3.0, R3.Pin_0
  N10: C4.-, J3.Line_2

custom parts:
  Terminal Block - 2 pins: Generic Screw Terminal 8mm
  Trimpot-#3296-flat: Bourns #3296 Square Trimpot 25 turn lying flat for low profile
