# Fritzing sketch CIRCUITO DE CONTROL LINEAL v2 (saved by Fritzing 1.0.3b)
circuit board: 5.0767cm x 6.64516cm
breadboards: 1

parts:
  J1 = Terminal Block - 3 pins [package=THT]
  D1 = Diode [package=diode-1n4148]
  D2 = Diode [package=diode-1n4148]
  D3 = Diode [package=diode-1n4148]
  D4 = Diode [package=diode-1n4148]
  R1 = Resistor [tolerance=±5% power=0.25W resistance=220 package=THT]
  R2 = Resistor [tolerance=±5% power=0.25W resistance=220 package=THT]
  Q1 = TRANSISTOR_NPN [package=to-92-ammo]
  Q2 = TRANSISTOR_NPN [package=to-92-ammo]
  R3 = Resistor [tolerance=±5% power=0.25W resistance=220 package=THT]
  R4 = Resistor [tolerance=±5% power=0.25W resistance=220 package=THT]
  P1 = Trimpot-3296 [package=3386u]
  R5 = Resistor [tolerance=±5% power=0.25W resistance=220 package=THT]
  R6 = Resistor [tolerance=±5% power=0.25W resistance=220 package=THT]
  P2 = Trimpot-3296 [package=3386u]
  R7 = Resistor [tolerance=±5% power=0.25W resistance=220 package=THT]
  P3 = Trimpot-3296 [package=3386u]
  R8 = Resistor [tolerance=±5% power=0.25W resistance=220 package=THT]
  P4 = Trimpot-3296 [package=3386u]
  J2 = Terminal Block - 2 pins [package=THT]
  J3 = Terminal Block - 2 pins [package=THT]
  J4 = Terminal Block - 2 pins [package=THT]
  J5 = Terminal Block - 2 pins [package=THT]
  LM7812 = Voltage Regulator [package=to220-igo]
  C3 = Electrolytic Capacitor [capacitance=1mF voltage=35V package="100 mil [THT, electrolytic]"]
  C2 = Electrolytic Capacitor [capacitance=1µF voltage=35V package="100 mil [THT, electrolytic]"]
  LM339 = IC, DIP package, 14 pins [chip_label=LM339]
  C1 = Electrolytic Capacitor [capacitance=1mF voltage=20V package="100 mil [THT, electrolytic]"]

nets:
  N1: J1.Line_1, D2.A, D4.A
  N2: J1.Line_2, R2.Pin_1, Q1.E, Q2.E, P1.CW, P2.CW, P3.CW, P4.CW, J2.Line_1, J3.Line_1, J4.Line_1, J5.Line_1, LM7812.GND, C3.-, C2.-, LM339.pin12, C1.-
  N3: J1.Line_3, D1.A, D3.A
  N4: D1.C, D2.C, LM7812.IN, C1.+
  N5: D3.C, D4.C, R1.Pin_0
  N6: R1.Pin_1, R2.Pin_0, Q1.B
  N7: Q1.C, Q2.B, R3.Pin_1
  N8: Q2.C, R4.Pin_1, C2.+, LM339.pin5, LM339.pin7, LM339.pin9, LM339.pin11
  N9: R3.Pin_0, R4.Pin_0, R5.Pin_0, R6.Pin_0, R7.Pin_0, R8.Pin_0, LM7812.OUT, C3.+, LM339.pin3
  N10: P1.CCW, R5.Pin_1
  N11: P1.WIPER, LM339.pin4
  N12: R6.Pin_1, P2.CCW
  N13: P2.WIPER, LM339.pin6
  N14: R7.Pin_1, P3.CCW
  N15: P3.WIPER, LM339.pin8
  N16: R8.Pin_1, P4.CCW
  N17: P4.WIPER, LM339.pin10
  N18: J2.Line_2, LM339.pin2
  N19: J3.Line_2, LM339.pin1
  N20: J4.Line_2, LM339.pin14
  N21: J5.Line_2, LM339.pin13

custom parts:
  Terminal Block - 3 pins: Generic Screw Terminal 9.5mm
  Trimpot-3296: Trimpot 3296 / 25 turn stand
  Terminal Block - 2 pins: Generic Screw Terminal 8mm
