# Fritzing sketch CIRCUITO DE CONTROL LINEAL (saved by Fritzing 1.0.3b)
circuit board: 7.10587cm x 8.12036cm
breadboards: 1

parts:
  J1 = Terminal Block - 3 pins [package=THT]
  D1 = Diode [package=diode-1n4148]
  D2 = Diode [package=diode-1n4148]
  D3 = Diode [package=diode-1n4148]
  D4 = Diode [package=diode-1n4148]
  R1 = Resistor [tolerance=±5% power=0.25W resistance=220 package=THT]
  R2 = Resistor [tolerance=±5% power=0.25W resistance=220 package=THT]
  Q1 = TRANSISTOR_NPN [package=to-92-ammo]
  Q2 = TRANSISTOR_NPN [package=to-92-ammo]
  R3 = Resistor [tolerance=±5% power=0.25W resistance=220 package=THT]
  R4 = Resistor [tolerance=±5% power=0.25W resistance=220 package=THT]
  P1 = Trimpot-3296 [package=3386u]
  R5 = Resistor [tolerance=±5% power=0.25W resistance=220 package=THT]
  LM339 = IC, DIP package, 14 pins [chip_label=LM339]
  R6 = Resistor [tolerance=±5% power=0.25W resistance=220 package=THT]
  P2 = Trimpot-3296 [package=3386u]
  R7 = Resistor [tolerance=±5% power=0.25W resistance=220 package=THT]
  P3 = Trimpot-3296 [package=3386u]
  R8 = Resistor [tolerance=±5% power=0.25W resistance=220 package=THT]
  P4 = Trimpot-3296 [package=3386u]
  R9 = Resistor [tolerance=±5% power=0.25W resistance=470 package=THT]
  R11 = Resistor [tolerance=±5% power=0.25W resistance=470 package=THT]
  R13 = Resistor [tolerance=±5% power=0.25W resistance=470 package=THT]
  R15 = Resistor [tolerance=±5% power=0.25W resistance=470 package=THT]
  R10 = Resistor [tolerance=±5% power=0.25W resistance=470 package=THT]
  R12 = Resistor [tolerance=±5% power=0.25W resistance=470 package=THT]
  R14 = Resistor [tolerance=±5% power=0.25W resistance=470 package=THT]
  R15_2 = Resistor [tolerance=±5% power=0.25W resistance=470 package=THT]
  J2 = Terminal Block - 2 pins [package=THT]
  J3 = Terminal Block - 2 pins [package=THT]
  J4 = Terminal Block - 2 pins [package=THT]
  J5 = Terminal Block - 2 pins [package=THT]
  LM7812 = Voltage Regulator [package=to220-igo]
  C1 = Electrolytic Capacitor [capacitance=1mF voltage=20V package="100 mil [THT, electrolytic]"]
  C3 = Electrolytic Capacitor [capacitance=1mF voltage=35V package="100 mil [THT, electrolytic]"]
  C2 = Electrolytic Capacitor [capacitance=1µF voltage=35V package="100 mil [THT, electrolytic]"]
  IC1 = IC, DIP package, 6 pins [chip_label=IC]
  IC2 = IC, DIP package, 6 pins [chip_label=IC]
  IC3 = IC, DIP package, 6 pins [chip_label=IC]
  IC4 = IC, DIP package, 6 pins [chip_label=IC]

nets:
  N1: J1.Line_1, D2.A, D4.A
  N2: J1.Line_2, R2.Pin_1, Q1.E, Q2.E, P1.CW, LM339.pin12, P2.CW, P3.CW, P4.CW, LM7812.GND, C1.-, C3.-, C2.-, IC1.pin2, IC2.pin2, IC3.pin2, IC4.pin2
  N3: J1.Line_3, D1.A, D3.A
  N4: D1.C, D2.C, LM7812.IN, C1.+
  N5: D3.C, D4.C, R1.Pin_0
  N6: R1.Pin_1, R2.Pin_0, Q1.B
  N7: Q1.C, Q2.B, R3.Pin_1
  N8: Q2.C, R4.Pin_1, LM339.pin5, LM339.pin7, LM339.pin9, LM339.pin11, C2.+
  N9: R3.Pin_0, R4.Pin_0, R5.Pin_0, LM339.pin3, R6.Pin_0, R7.Pin_0, R8.Pin_0, R9.Pin_0, R11.Pin_0, R13.Pin_0, R15.Pin_0, LM7812.OUT, C3.+
  N10: P1.CCW, R5.Pin_1
  N11: P1.WIPER, LM339.pin6
  N12: LM339.pin1, R11.Pin_1, R12.Pin_1
  N13: LM339.pin2, R9.Pin_1, R10.Pin_1
  N14: LM339.pin4, P2.WIPER
  N15: LM339.pin8, P3.WIPER
  N16: LM339.pin10, P4.WIPER
  N17: LM339.pin13, R15.Pin_1, R15_2.Pin_1
  N18: LM339.pin14, R13.Pin_1, R14.Pin_1
  N19: R6.Pin_1, P2.CCW
  N20: R7.Pin_1, P3.CCW
  N21: R8.Pin_1, P4.CCW
  N22: R10.Pin_0, IC1.pin1
  N23: R12.Pin_0, IC2.pin1
  N24: R14.Pin_0, IC3.pin1
  N25: R15_2.Pin_0, IC4.pin1
  N26: J2.Line_1, IC1.pin4
  N27: J2.Line_2, IC1.pin6
  N28: J3.Line_1, IC2.pin4
  N29: J3.Line_2, IC2.pin6
  N30: J4.Line_1, IC3.pin4
  N31: J4.Line_2, IC3.pin6
  N32: J5.Line_1, IC4.pin4
  N33: J5.Line_2, IC4.pin6

custom parts:
  Terminal Block - 3 pins: Generic Screw Terminal 9.5mm
  Trimpot-3296: Trimpot 3296 / 25 turn stand
  Terminal Block - 2 pins: Generic Screw Terminal 8mm
