# Fritzing sketch Untitled Sketch (saved by Fritzing 0.9.10b)
circuit board: 3.25616cm x 2.50101cm
breadboards: 1

parts:
  R1 = Resistor [tolerance=±5% power=0.25 resistance=220 package=THT]
  LED1 = LED - 5mm [color="Red (633nm)" current=0.030 package="5 mm [THT]"]
  VCC1 = Battery

nets:
  5V: R1.Pin_0, VCC1.+
  N1: R1.Pin_1, LED1.anode
  GND: LED1.cathode, VCC1.-
