# Fritzing sketch L239D (saved by Fritzing 0.9.10b)
circuit board: 7.6865cm x 4.01908cm
breadboards: 1

parts:
  IC1 = IC, DIP package, 16 pins [chip_label=IC]
  VCC-GND = female alternating pin header, 2 pins [form="♀ (female)"]
  J2 = female pin header, 2 pins [form="♀ (female)"]
  J3 = female pin header, 2 pins [form="♀ (female)"]
  J4 = female pin header, 2 pins [form="♀ (female)"]
  J5 = female pin header, 2 pins [form="♀ (female)"]
  J6 = female pin header, 2 pins [form="♀ (female)"]
  IC2 = IC, DIP package, 16 pins [chip_label=IC]
  J7 = female pin header, 2 pins [form="♀ (female)"]
  J8 = female pin header, 2 pins [form="♀ (female)"]
  J9 = female pin header, 2 pins [form="♀ (female)"]
  J10 = female pin header, 2 pins [form="♀ (female)"]
  J11 = female pin header, 2 pins [form="♀ (female)"]

nets:
  N1: IC1.pin1, J2.pin1
  N2: IC1.pin2, J3.pin1
  N3: IC1.pin3, J3.pin2
  N4: IC1.pin4, IC1.pin5, IC1.pin12, IC1.pin13, VCC-GND.pin2, IC2.pin4, IC2.pin5, IC2.pin12, IC2.pin13
  N5: IC1.pin6, J4.pin1
  N6: IC1.pin7, J4.pin2
  N7: IC1.pin8, IC1.pin16, VCC-GND.pin1, IC2.pin8, IC2.pin16
  N8: IC1.pin9, J2.pin2
  N9: IC1.pin10, J6.pin2
  N10: IC1.pin11, J6.pin1
  N11: IC1.pin14, J5.pin2
  N12: IC1.pin15, J5.pin1
  N13: IC2.pin1, J7.pin1
  N14: IC2.pin2, J8.pin1
  N15: IC2.pin3, J8.pin2
  N16: IC2.pin6, J9.pin1
  N17: IC2.pin7, J9.pin2
  N18: IC2.pin9, J7.pin2
  N19: IC2.pin10, J11.pin2
  N20: IC2.pin11, J11.pin1
  N21: IC2.pin14, J10.pin2
  N22: IC2.pin15, J10.pin1
