# Fritzing sketch SEGUIDOR_DE_VOLTAJE (saved by Fritzing 0.9.10b)
circuit board: 3.80025cm x 4.3139cm
breadboards: 1

parts:
  LM358 = LM358 [package=dip08]
  R1 = Resistor [tolerance=±5% power=0.25 resistance=220 package=THT]
  R2 = Resistor [tolerance=±10% power=0.25 resistance=220 package=THT]
  R3 = Resistor [tolerance=±5% power=0.25 resistance=220 package=THT]
  R4 = Resistor [tolerance=±5% power=0.25 resistance=220 package=THT]
  J3 = female pin header, 2 pins [form="♀ (female)"]
  J1 = female pin header, 3 pins [form="♀ (female)"]
  J2 = female pin header, 2 pins [form="♀ (female)"]
  J4 = female pin header, 2 pins [form="♀ (female)"]
  J5 = female pin header, 2 pins [form="♀ (female)"]

nets:
  N1: LM358.G$1_OUT, R4.Pin_1, J5.pin1
  N2: LM358.G$1_-IN, R3.Pin_0, R4.Pin_0
  N3: LM358.G$1_+IN, J3.pin1
  N4: LM358.G$1_V-, J1.pin2
  N5: LM358.G$2_+IN, J2.pin1
  N6: LM358.G$2_-IN, R1.Pin_0, R2.Pin_0
  N7: LM358.G$2_OUT, R1.Pin_1, J4.pin1
  N8: LM358.G$1_V+, J1.pin1
  N9: R2.Pin_1, R3.Pin_1, J3.pin2, J1.pin3, J2.pin2, J4.pin2, J5.pin2
