# Fritzing sketch RECEPTOR AM (saved by Fritzing 1.0.3b)
circuit board: 4.32cm x 4.32cm
breadboards: 1

parts:
  C1 = Electrolytic Capacitor [capacitance=1µF voltage=35V package="100 mil [THT, electrolytic]"]
  C2 = Electrolytic Capacitor [capacitance=1µF voltage=35V package="100 mil [THT, electrolytic]"]
  J2 = Terminal Block - 3 pins [package=THT]
  R1 = Resistor [tolerance=±5% power=0.25W resistance=220 package=THT]
  R2 = Resistor [tolerance=±5% power=0.25W resistance=220 package=THT]
  R3 = Resistor [tolerance=±5% power=0.25W resistance=220 package=THT]
  LM741 = LM741 [part_number=LM741 package="DIP (Dual Inline) [THT]"]
  R4 = Resistor [tolerance=±5% power=0.25W resistance=220 package=THT]
  VR1 = Trimpot-3296 [package=3386u]
  LM386 = IC, DIP package, 8 pins [chip_label=IC]
  J3 = Terminal Block - 2 pins [package=THT]
  LED1 = LED - 5mm [color="Red (633nm)" current=0.030A package="5 mm [THT]"]
  C3 = Electrolytic Capacitor [capacitance=1µF voltage=35V package="100 mil [THT, electrolytic]"]
  C4 = Electrolytic Capacitor [capacitance=1µF voltage=35V package="100 mil [THT, electrolytic]"]

nets:
  N1: C1.-, C2.-, J2.Line_2, R4.Pin_1, VR1.CW, LM386.pin2, LM386.pin4, LED1.cathode
  N2: C1.+, J2.Line_1, R1.Pin_0, LM386.pin6, J3.Line_2
  N3: C2.+, J2.Line_3, LM741.pin4
  N4: R1.Pin_1, LM741.pin7, C4.+
  N5: R2.Pin_0, C4.-
  N6: R2.Pin_1, R3.Pin_0, LM741.pin2, LED1.anode
  N7: R3.Pin_1, LM741.pin6, VR1.CCW
  N8: LM741.pin3, R4.Pin_0
  N9: VR1.WIPER, LM386.pin3
  N10: LM386.pin5, C3.+
  N11: J3.Line_1, C3.-

custom parts:
  Terminal Block - 3 pins: Generic Screw Terminal 8mm
  LM741: This is a single Op Amp DIP.
  Trimpot-3296: Trimpot 3296 / 25 turn stand
  Terminal Block - 2 pins: Generic Screw Terminal 8mm
