# Fritzing sketch TRANSMISOR AM (saved by Fritzing 1.0.3b)
circuit board: 4.57cm x 4.57cm
breadboards: 1

parts:
  LM741 = LM741 [part_number=LM741 package="DIP (Dual Inline) [THT]"]
  C1 = Electrolytic Capacitor [capacitance=1µF voltage=35V package="100 mil [THT, electrolytic]"]
  C2 = Electrolytic Capacitor [capacitance=1µF voltage=35V package="100 mil [THT, electrolytic]"]
  R1 = Resistor [tolerance=±5% power=0.25W resistance=220 package=THT]
  MIC = Microphone
  R2 = Resistor [tolerance=±5% power=0.25W resistance=220 package=THT]
  VR2 = Trimpot-3296 [package=3386u]
  R4 = Resistor [tolerance=±5% power=0.25W resistance=220 package=THT]
  R6 = Resistor [tolerance=±5% power=0.25W resistance=220 package=THT]
  J1 = Terminal Block - 3 pins [package=THT]
  R5 = Resistor [tolerance=±5% power=0.25W resistance=220 package=THT]
  VR1 = Trimpot-3296 [package=3386u]
  2N2222 = TRANSISTOR_NPN [package=to-92-ammo]
  C5 = Electrolytic Capacitor [capacitance=1µF voltage=35V package="100 mil [THT, electrolytic]"]
  C6 = Electrolytic Capacitor [capacitance=1µF voltage=35V package="100 mil [THT, electrolytic]"]
  LED1 = LED - 5mm [color="Red (633nm)" current=0.030A package="5 mm [THT]"]
  R3 = Resistor [tolerance=±5% power=0.25W resistance=220 package=THT]

nets:
  N1: LM741.pin2, R2.Pin_0, VR1.CCW
  N2: LM741.pin3, R3.Pin_0
  N3: LM741.pin4, C2.+, J1.Line_3
  N4: LM741.pin6, VR1.WIPER
  N5: LM741.pin7, C1.+, R1.Pin_1, R4.Pin_1, J1.Line_1, R5.Pin_1
  N6: C1.-, C2.-, MIC.pin2, R6.Pin_0, J1.Line_2, LED1.cathode, R3.Pin_1
  N7: R1.Pin_0, MIC.pin1, C6.+
  N8: R2.Pin_1, C6.-
  N9: VR2.CCW, R6.Pin_1
  N10: VR2.WIPER, 2N2222.B, C5.-
  N11: VR2.CW, R4.Pin_0
  N12: R5.Pin_0, 2N2222.C
  N13: VR1.CW, C5.+
  N14: 2N2222.E, LED1.anode

custom parts:
  LM741: This is a single Op Amp DIP.
  Trimpot-3296: Trimpot 3296 / 25 turn stand
  Terminal Block - 3 pins: Generic Screw Terminal 8mm
